// Logisim project ALU.circ as structural Verilog: 1 circuit, main circuit ALU
module ALU (
  input  [31:0] A,
  input  [31:0] B,
  input  [4:0] Shift,
  input  [3:0] Codop,
  input  CarryIn,
  output [31:0] S,
  output [3:0] Flags
);

  wire CARRYOUT_ADC, CARRYOUT_ASR, CARRYOUT_CMN, CARRYOUT_CMP, CARRYOUT_LSL, CARRYOUT_LSR, CARRYOUT_ROR,
       CARRYOUT_SBC, CMN_31, CMP_31, not_1_out, not_4_out, not_7_out, OVERFLOW_ADC, OVERFLOW_CMN,
       OVERFLOW_CMP, OVERFLOW_SBC, subtractor_1_bout, subtractor_3_bout, xnor_1_out, xnor_2_out, xnor_3_out,
       xnor_4_out, xor_2_out, xor_3_out, xor_4_out, xor_5_out;
  wire [4:0] subtractor_4_out, subtractor_5_out, subtractor_6_out;
  wire [30:0] CMN_flags, CMP_flags, RROR, shifter_5_out;
  wire [31:0] AAND, ADC, ASR, BIC, EOR, LSL, LSR, MUL, multiplexer_2_out, MVN, not_2_out, ORR, RSB, SBC, TST;
  wire [31:1] shifter_6_out, shifter_7_out;

  not not_1 (not_1_out, A[31]);
  assign not_2_out = ~A;  // NOT_Gate not_2, 32 bits wide
  assign MVN = ~B;  // NOT_Gate not_3, 32 bits wide
  assign AAND = A & B;  // AND_Gate and_1, 32 bits wide
  assign EOR = A ^ B;  // XOR_Gate xor_1, 32 bits wide
  Shifter #(.width(32)) shifter_1 (.in(B), .\dist (Shift), .out(LSL));
  Shifter #(.shift("lr"), .width(32)) shifter_2 (.in(B), .\dist (Shift), .out(LSR));
  Shifter #(.shift("ar"), .width(32)) shifter_3 (.in(B), .\dist (Shift), .out(ASR));
  Adder #(.width(32)) adder_1 (.a(A), .b(B), .out(ADC), .cin(CarryIn), .cout(CARRYOUT_ADC));
  not not_4 (not_4_out, CarryIn);
  Subtractor #(.width(32)) subtractor_1 (.a(B), .b(A), .out(SBC), .bin(not_4_out), .bout(subtractor_1_bout));
  not not_5 (CARRYOUT_SBC, subtractor_1_bout);
  Shifter #(.shift("rr"), .width(32)) shifter_4 (.in(B), .\dist (Shift), .out({CARRYOUT_ROR, RROR}));
  assign TST = A & B;  // AND_Gate and_2, 32 bits wide
  Subtractor #(.width(32)) subtractor_2 (.a({32{1'b0}}), .b(A), .out(RSB));  // open: bin, bout
  Subtractor #(.width(32)) subtractor_3 (
    .a(B), .b(A), .out({CMP_31, CMP_flags}), .bout(subtractor_3_bout));  // open: bin
  not not_6 (CARRYOUT_CMP, subtractor_3_bout);
  Adder #(.width(32)) adder_2 (.a(A), .b(B), .out({CMN_31, CMN_flags}), .cout(CARRYOUT_CMN));  // open: cin
  assign ORR = A | B;  // OR_Gate or_1, 32 bits wide
  Multiplier #(.width(32)) multiplier_1 (.a(A), .b(B), .out(MUL));  // open: cin, cout
  assign BIC = B & not_2_out;  // AND_Gate and_3, 32 bits wide
  xnor xnor_1 (xnor_1_out, A[31], B[31]);
  xor xor_2 (xor_2_out, B[31], ADC[31]);
  xnor xnor_2 (xnor_2_out, B[31], not_1_out);
  xor xor_3 (xor_3_out, not_1_out, SBC[31]);
  and and_4 (OVERFLOW_ADC, xnor_1_out, xor_2_out);
  and and_5 (OVERFLOW_SBC, xnor_2_out, xor_3_out);
  Subtractor #(.width(5)) subtractor_4 (.a(Shift), .b(5'b00001), .out(subtractor_4_out));  // open: bin, bout
  Subtractor #(.width(5)) subtractor_5 (.a(Shift), .b(5'b00001), .out(subtractor_5_out));  // open: bin, bout
  Subtractor #(.width(5)) subtractor_6 (.a(Shift), .b(5'b00001), .out(subtractor_6_out));  // open: bin, bout
  Shifter #(.shift("lr"), .width(32)) shifter_5 (
    .in(A), .\dist (subtractor_4_out), .out({CARRYOUT_LSL, shifter_5_out}));
  Shifter #(.shift("lr"), .width(32)) shifter_6 (
    .in(A), .\dist (subtractor_5_out), .out({shifter_6_out, CARRYOUT_LSR}));
  Shifter #(.shift("ar"), .width(32)) shifter_7 (
    .in(A), .\dist (subtractor_6_out), .out({shifter_7_out, CARRYOUT_ASR}));
  not not_7 (not_7_out, A[31]);
  xnor xnor_3 (xnor_3_out, B[31], not_7_out);
  xor xor_4 (xor_4_out, not_7_out, CMP_31);
  xnor xnor_4 (xnor_4_out, A[31], B[31]);
  xor xor_5 (xor_5_out, B[31], CMN_31);
  and and_6 (OVERFLOW_CMP, xnor_3_out, xor_4_out);
  and and_7 (OVERFLOW_CMN, xnor_4_out, xor_5_out);
  Multiplexer #(.enable("false"), .select(4), .width(32)) multiplexer_1 (
    .in0(AAND), .in1(EOR), .in2(LSL), .in3(LSR), .in4(ASR), .in5(ADC), .in6(SBC), .in7({CARRYOUT_ROR, RROR}),
    .in8(TST), .in9(RSB), .in10(B), .in11(B), .in12(ORR), .in13(MUL), .in14(BIC), .in15(MVN), .out(S),
    .sel(Codop));
  Multiplexer #(.enable("false"), .select(4), .width(32)) multiplexer_2 (
    .in0(S), .in1(S), .in2(S), .in3(S), .in4(S), .in5(S), .in6(S), .in7(S), .in8(S), .in9(S),
    .in10({CMP_31, CMP_flags}), .in11({CMN_31, CMN_flags}), .in12(S), .in13(S), .in14(S), .in15(S),
    .out(multiplexer_2_out), .sel(Codop));
  Multiplexer #(.enable("false"), .select(4)) multiplexer_3 (
    .in0(1'b0), .in1(1'b0), .in2(1'b0), .in3(1'b0), .in4(1'b0), .in5(OVERFLOW_ADC), .in6(OVERFLOW_SBC),
    .in7(1'b0), .in8(1'b0), .in9(1'b0), .in10(OVERFLOW_CMP), .in11(OVERFLOW_CMN), .in12(1'b0), .in13(1'b0),
    .in14(1'b0), .in15(1'b0), .out(Flags[0]), .sel(Codop));
  Multiplexer #(.enable("false"), .select(4)) multiplexer_4 (
    .in0(1'b0), .in1(1'b0), .in2(CARRYOUT_LSL), .in3(CARRYOUT_LSR), .in4(CARRYOUT_ASR), .in5(CARRYOUT_ADC),
    .in6(CARRYOUT_SBC), .in7(CARRYOUT_ROR), .in8(1'b0), .in9(1'b0), .in10(CARRYOUT_CMP), .in11(CARRYOUT_CMN),
    .in12(1'b0), .in13(1'b0), .in14(1'b0), .in15(1'b0), .out(Flags[1]), .sel(Codop));
  Comparator #(.width(32)) comparator_1 (
    .a(multiplexer_2_out), .b({32{1'b0}}), .eq(Flags[2]), .lt(Flags[3]));  // open: gt

  // Other names for the same wires on the sheet: A_31 = A[31]; ADC_31 = ADC[31]; CMN_flags[31] = CMN_31;
  //   CMN[31:0] = B; CMP[31:0] = B; B_31 = B[31]; CMP_flags[31] = CMP_31; V = Flags[0]; C = Flags[1]; Z = Flags[2];
  //   N = Flags[3]; RROR[31] = CARRYOUT_ROR; SBC_31 = SBC[31]; Sortie[31:0] = S

  // Notes on the sheet:
  //   Note: for ROR, C = N
  //   Note 2: assume that shift > 0 for LSL and LSR
endmodule
