// Logisim project Ctl_Load_Store.circ as structural Verilog: 1 circuit, main circuit Load_Store
module Load_Store (
  input  Enable,
  input  [15:0] Instruction,
  input  Clk,
  input  Reset,
  input  [31:0] Stack_Pointer,
  output Store,
  output Load,
  output PC_Hold,
  output [2:0] Rmd,
  output [31:0] RAM_Addr
);

  wire d_ff_1_qn, load_t, store_t;
  wire [2:0] rmd_t;
  wire [7:0] shifter_1_out;
  wire [31:0] bit_extender_1_out, ram_addr_t;

  Decoder #(.enable("false")) decoder_1 (.out0(store_t), .out1(load_t), .sel(Instruction[11]));
  Shifter shifter_1 (.in(Instruction[7:0]), .\dist (3'b010), .out(shifter_1_out));
  assign bit_extender_1_out = {{24{shifter_1_out[7]}}, shifter_1_out};  // Bit_Extender bit_extender_1
  D_Flip_Flop d_ff_1 (.clk(Clk), .Qn(d_ff_1_qn), .preset(load_t), .reset(Reset));  // open: D, Q
  Adder #(.width(32)) adder_1 (.a(Stack_Pointer), .b(bit_extender_1_out), .out(ram_addr_t));  // open: cin, cout
  Pull_Resistor pull_resistor_1 (.node(Store));
  assign Store = Enable ? store_t : 1'bz;  // Controlled_Buffer controlled_buffer_1
  Pull_Resistor pull_resistor_2 (.node(Load));
  assign Load = Enable ? load_t : 1'bz;  // Controlled_Buffer controlled_buffer_2
  Pull_Resistor pull_resistor_3 (.node(PC_Hold));
  assign PC_Hold = Enable ? d_ff_1_qn : 1'bz;  // Controlled_Buffer controlled_buffer_3
  Pull_Resistor pull_resistor_4 (.node(Rmd));
  assign Rmd = Enable ? rmd_t : 3'bz;  // Controlled_Buffer controlled_buffer_4
  Pull_Resistor pull_resistor_5 (.node(RAM_Addr));
  assign RAM_Addr = Enable ? ram_addr_t : 32'bz;  // Controlled_Buffer controlled_buffer_5
  D_Flip_Flop d_ff_2 (.clk(Clk), .reset(Reset));  // open: D, Q, Qn, preset

  // Other names for the same wires on the sheet: imm8[7:0] = Instruction[7:0]; Rt[2:0] = Instruction[10:8];
  //   opcode = Instruction[11]; SP[31:0] = Stack_Pointer

  // Notes on the sheet:
  //   Instruction: pull=down
  //   store / load
  //   Delay load and hold PC for 1 cycle for the RAM to send out requested data 
endmodule
