// Logisim project Ctl_Shift_Add_Sub_Mov.circ as structural Verilog: 1 circuit, main circuit Shift_Add_Sub_Mov
module Shift_Add_Sub_Mov (
  input  Enable,
  input  [15:0] Instruction,
  output [3:0] Flags_Update_Mask,
  output Carry,
  output Imm32_Enable,
  output [2:0] Rm,
  output [2:0] Rn,
  output [2:0] Rd,
  output [4:0] Imm5,
  output [31:0] Imm32,
  output [3:0] ALU_Opcode
);

  wire carry_t, comparator_1_gt, comparator_2_gt, multiplexer_6_out, or_1_out;
  wire [2:0] imm3, multiplexer_2_out, multiplexer_4_out, Rd_t, Rm_t, Rn_t;
  wire [3:0] flags, multiplexer_5_out, multiplexer_8_out;
  wire [4:0] I6_10, imm5_t;
  wire [7:0] imm8, not_1_out;
  wire [31:0] imm32_t;

  Multiplexer #(.enable("false"), .select(3), .width(3)) multiplexer_1 (
    .in3(Instruction[5:3]), .out(Rn_t), .sel(Instruction[13:11]));  // open: in0, in1, in2, in4, in5, in6, in7
  Multiplexer #(.enable("false"), .select(2), .width(3)) multiplexer_2 (
    .in2(Instruction[8:6]), .in3(Instruction[8:6]), .out(multiplexer_2_out), .sel(Instruction[10:9]));  // open: in0, in1
  assign imm32_t = {{29{imm3[2]}}, imm3};  // Bit_Extender bit_extender_1
  assign imm32_t = {{24{imm8[7]}}, imm8};  // Bit_Extender bit_extender_2
  Multiplexer #(.enable("false"), .select(3), .width(3)) multiplexer_3 (
    .in3(multiplexer_2_out), .out(imm3), .sel(Instruction[13:11]));  // open: in0, in1, in2, in4, in5, in6, in7
  Multiplexer #(.enable("false"), .select(2), .width(3)) multiplexer_4 (
    .in0(Instruction[8:6]), .in1(Instruction[8:6]), .out(multiplexer_4_out), .sel(Instruction[10:9]));  // open: in2, in3
  Multiplexer #(.enable("false"), .select(2), .width(4)) multiplexer_5 (
    .in0(4'b0101), .in1(4'b0110), .in2(4'b0101), .in3(4'b0110), .out(multiplexer_5_out),
    .sel(Instruction[10:9]));
  Comparator #(.width(3)) comparator_1 (.a(imm3), .b(3'b000), .gt(comparator_1_gt));  // open: eq, lt
  Comparator comparator_2 (.a(imm8), .b({8{1'b0}}), .gt(comparator_2_gt));  // open: eq, lt
  Multiplexer #(.enable("false"), .select(2)) multiplexer_6 (
    .in0(1'b0), .in1(1'b1), .in2(1'b0), .in3(1'b1), .out(multiplexer_6_out), .sel(Instruction[10:9]));
  Multiplexer #(.enable("false"), .select(3)) multiplexer_7 (
    .in3(multiplexer_6_out), .out(carry_t), .sel(Instruction[13:11]));  // open: in0, in1, in2, in4, in5, in6, in7
  assign Flags_Update_Mask = Enable ? flags : 4'bz;  // Controlled_Buffer controlled_buffer_1
  assign Carry = Enable ? carry_t : 1'bz;  // Controlled_Buffer controlled_buffer_2
  or or_1 (or_1_out, comparator_1_gt, comparator_2_gt);
  assign Imm32_Enable = Enable ? or_1_out : 1'bz;  // Controlled_Buffer controlled_buffer_3
  assign Rm = Enable ? Rm_t : 3'bz;  // Controlled_Buffer controlled_buffer_4
  assign Rn = Enable ? Rn_t : 3'bz;  // Controlled_Buffer controlled_buffer_5
  Multiplexer #(.enable("false"), .select(3), .width(4)) multiplexer_8 (
    .in0(4'b0010), .in1(4'b0011), .in2(4'b0100), .in3(multiplexer_5_out), .in4(4'b1001), .in5(4'b1010),
    .in6(4'b0101), .in7(4'b0110), .out(multiplexer_8_out), .sel(Instruction[13:11]));
  Multiplexer #(.enable("false"), .select(3), .width(3)) multiplexer_9 (
    .in0(Instruction[5:3]), .in1(Instruction[5:3]), .in2(Instruction[5:3]), .in3(multiplexer_4_out),
    .out(Rm_t), .sel(Instruction[13:11]));  // open: in4, in5, in6, in7
  Multiplexer #(.enable("false"), .select(3), .width(5)) multiplexer_10 (
    .in0(I6_10), .in1(I6_10), .in2(I6_10), .out(imm5_t), .sel(Instruction[13:11]));  // open: in3, in4, in5, in6, in7
  Pull_Resistor pull_resistor_1 (.node(Flags_Update_Mask));
  Pull_Resistor pull_resistor_2 (.node(Carry));
  Pull_Resistor pull_resistor_3 (.node(Imm32_Enable));
  Pull_Resistor pull_resistor_4 (.node(Rm));
  Pull_Resistor pull_resistor_5 (.node(Rn));
  Pull_Resistor pull_resistor_6 (.node(Rd));
  assign Rd = Enable ? Rd_t : 3'bz;  // Controlled_Buffer controlled_buffer_6
  Pull_Resistor pull_resistor_7 (.node(Imm5));
  assign Imm5 = Enable ? imm5_t : 5'bz;  // Controlled_Buffer controlled_buffer_7
  Pull_Resistor pull_resistor_8 (.node(Imm32));
  assign Imm32 = Enable ? imm32_t : 32'bz;  // Controlled_Buffer controlled_buffer_8
  Pull_Resistor pull_resistor_9 (.node(ALU_Opcode));
  assign ALU_Opcode = Enable ? multiplexer_8_out : 4'bz;  // Controlled_Buffer controlled_buffer_9
  assign not_1_out = ~Instruction[7:0];  // NOT_Gate not_1, 8 bits wide
  Multiplexer #(.enable("false"), .select(3), .width(4)) multiplexer_11 (
    .in0(4'b1101), .in1(4'b1101), .in2(4'b1101), .in3(4'b1110), .in4(4'b1100), .in5(4'b1110), .in6(4'b1110),
    .in7(4'b1110), .out(flags), .sel(Instruction[13:11]));
  Multiplexer #(.enable("false"), .select(3), .width(3)) multiplexer_12 (
    .in0(Instruction[2:0]), .in1(Instruction[2:0]), .in2(Instruction[2:0]), .in3(Instruction[2:0]),
    .in4(Instruction[10:8]), .in5(Instruction[10:8]), .in6(Instruction[10:8]), .in7(Instruction[10:8]),
    .out(Rd_t), .sel(Instruction[13:11]));
  Multiplexer #(.enable("false"), .select(3), .width(8)) multiplexer_13 (
    .in4(not_1_out), .in5(Instruction[7:0]), .in6(Instruction[7:0]), .in7(Instruction[7:0]), .out(imm8),
    .sel(Instruction[13:11]));  // open: in0, in1, in2, in3

  // Other names for the same wires on the sheet: I0 = Instruction[0]; I0_2[2:0] = Instruction[2:0];
  //   I0_7[7:0] = Instruction[7:0]; I1 = Instruction[1]; I2 = Instruction[2]; I3 = Instruction[3];
  //   I3_5[2:0] = Instruction[5:3]; I4 = Instruction[4]; I5 = Instruction[5]; I6 = Instruction[6];
  //   I6_8[2:0] = Instruction[8:6]; I7 = Instruction[7]; I8 = Instruction[8]; I8_10[2:0] = Instruction[10:8];
  //   I9 = Instruction[9]; opcode2[1:0] = Instruction[10:9]; I10 = Instruction[10]; I14 = Instruction[14];
  //   I15 = Instruction[15]; I11 = Instruction[11]; opcode1[2:0] = Instruction[13:11]; I12 = Instruction[12];
  //   I13 = Instruction[13]

  // Notes on the sheet:
  //   Pull output low on Enable = 0
  //   Enable carry for SUB since it is reversed in ALU
  //   ALU will use Imm32 instead of Rm
  //   only ADD and SUB use Rm
  //   Note: ALU uses Rn register for shifts. Use Rn instead of Rm for shifts (immediate) here too
  //   Note 2: MOV uses RSB ALU opcode with Imm8 reversed so that it is copied to output register
  //   Note 3: Imm32_Enable forces the use of the immediate for Rm register
endmodule
