// Logisim project BancDeRegistres.circ as structural Verilog: 1 circuit, main circuit BancRegistre
module BancRegistre (
  input  [31:0] DataIn,
  input  Clk,
  input  Reset,
  input  [2:0] RegDest,
  input  [2:0] RegA,
  input  [2:0] RegB,
  output [31:0] R0,
  output [31:0] R1,
  output [31:0] R2,
  output [31:0] R3,
  output [31:0] AOut,
  output [31:0] R4,
  output [31:0] R5,
  output [31:0] BOut,
  output [31:0] R6,
  output [31:0] R7
);

  wire R0_t, R1_t, R2_t, R3_t, R4_t, R5_t, R6_t, R7_t;

  Decoder #(.select(3)) decoder_1 (
    .out0(R0_t), .out1(R1_t), .out2(R2_t), .out3(R3_t), .out4(R4_t), .out5(R5_t), .out6(R6_t), .out7(R7_t),
    .sel(RegDest));  // open: en
  Multiplexer #(.enable("false"), .select(3), .width(32)) multiplexer_1 (
    .in0(R0), .in1(R1), .in2(R2), .in3(R3), .in4(R4), .in5(R5), .in6(R6), .in7(R7), .out(AOut), .sel(RegA));
  Multiplexer #(.enable("false"), .select(3), .width(32)) multiplexer_2 (
    .in0(R0), .in1(R1), .in2(R2), .in3(R3), .in4(R4), .in5(R5), .in6(R6), .in7(R7), .out(BOut), .sel(RegB));
  Register #(.width(32)) register_1 (.D(DataIn), .en(R0_t), .clk(Clk), .Q(R0), .clr(Reset));
  Register #(.width(32)) register_2 (.D(DataIn), .en(R1_t), .clk(Clk), .Q(R1), .clr(Reset));
  Register #(.width(32)) register_3 (.D(DataIn), .en(R2_t), .clk(Clk), .Q(R2), .clr(Reset));
  Register #(.width(32)) register_4 (.D(DataIn), .en(R3_t), .clk(Clk), .Q(R3), .clr(Reset));
  Register #(.width(32)) register_5 (.D(DataIn), .en(R4_t), .clk(Clk), .Q(R4), .clr(Reset));
  Register #(.width(32)) register_6 (.D(DataIn), .en(R5_t), .clk(Clk), .Q(R5), .clr(Reset));
  Register #(.width(32)) register_7 (.D(DataIn), .en(R6_t), .clk(Clk), .Q(R6), .clr(Reset));
  Register #(.width(32)) register_8 (.D(DataIn), .en(R7_t), .clk(Clk), .Q(R7), .clr(Reset));

  // Other names for the same wires on the sheet: Clock = Clk; S0[31:0] = R0; S1[31:0] = R1; S2[31:0] = R2;
  //   S3[31:0] = R3; S4[31:0] = R4; S5[31:0] = R5; S6[31:0] = R6; S7[31:0] = R7
endmodule
