// Logisim project Ctl_Conditional.circ as structural Verilog: 1 circuit, main circuit Conditional
module Conditional (
  input  Enable,
  input  [15:0] Instruction,
  input  N,
  input  Z,
  input  C,
  input  V,
  output [10:0] Offset,
  output Verified
);

  wire CC, CS, EQ, GE, GT, HI, LE, LS, LT, MI, multiplexer_2_out, NE, PL, VC, verif, VS;
  wire [10:0] bit_extender_1_out;

  assign bit_extender_1_out = {{3{Instruction[7]}}, Instruction[7:0]};  // Bit_Extender bit_extender_1
  Multiplexer #(.width(11)) multiplexer_1 (
    .in0(bit_extender_1_out), .in1(Instruction[10:0]), .out(Offset), .sel(Instruction[13]));
  Multiplexer multiplexer_2 (.in0(verif), .in1(1'b1), .out(multiplexer_2_out), .sel(Instruction[13]));
  Comparator #(.width(1)) comparator_1 (.a(Z), .b(1'b1), .eq(EQ));  // open: gt, lt
  Comparator #(.width(1)) comparator_2 (.a(Z), .b(1'b0), .eq(NE));  // open: gt, lt
  Comparator #(.width(1)) comparator_3 (.a(C), .b(1'b1), .eq(CS));  // open: gt, lt
  Comparator #(.width(1)) comparator_4 (.a(C), .b(1'b0), .eq(CC));  // open: gt, lt
  Comparator #(.width(1)) comparator_5 (.a(N), .b(1'b1), .eq(MI));  // open: gt, lt
  Comparator #(.width(1)) comparator_6 (.a(N), .b(1'b0), .eq(PL));  // open: gt, lt
  Comparator #(.width(1)) comparator_7 (.a(V), .b(1'b1), .eq(VS));  // open: gt, lt
  Comparator #(.width(1)) comparator_8 (.a(V), .b(1'b0), .eq(VC));  // open: gt, lt
  and and_1 (HI, CS, NE);
  or or_1 (LS, CC, EQ);
  Comparator #(.width(1)) comparator_9 (.a(N), .b(V), .eq(GE));  // open: gt, lt
  and and_2 (GT, NE, GE);
  or or_2 (LE, EQ, LT);
  Pull_Resistor pull_resistor_1 (.node(Verified));
  assign Verified = Enable ? multiplexer_2_out : 1'bz;  // Controlled_Buffer controlled_buffer_1
  not not_1 (LT, GE);
  Multiplexer #(.select(4)) multiplexer_3 (
    .in0(EQ), .in1(NE), .in2(CS), .in3(CC), .in4(MI), .in5(PL), .in6(VS), .in7(VC), .in8(HI), .in9(LS),
    .in10(GE), .in11(LT), .in12(GT), .in13(LE), .in14(1'b1), .in15(1'b0), .out(verif), .sel(Instruction[11:8]));

  // Other names for the same wires on the sheet: imm8[7:0] = Instruction[7:0]; imm11[10:0] = Instruction[10:0];
  //   Cond[3:0] = Instruction[11:8]; bit_13 = Instruction[13]
endmodule
