// Logisim project Ctl_Data_Processing.circ as structural Verilog: 1 circuit, main circuit Data_Processing
module Data_Processing (
  input  Enable,
  input  [15:0] Instruction,
  output [2:0] Rd,
  output [2:0] Rn,
  output [2:0] Rm,
  output [3:0] ALU_Opcode,
  output [3:0] Flags_Update_Mask
);

  wire [2:0] Rd_t, Rm_t, Rn_t;
  wire [3:0] Flags;

  Multiplexer #(.enable("false"), .select(4), .width(3)) multiplexer_1 (
    .in0(Instruction[2:0]), .in1(Instruction[2:0]), .in2(Instruction[2:0]), .in3(Instruction[2:0]),
    .in4(Instruction[2:0]), .in5(Instruction[2:0]), .in6(Instruction[2:0]), .in7(Instruction[2:0]),
    .in8(3'b000), .in9(Instruction[2:0]), .in10(3'b000), .in11(3'b000), .in12(Instruction[2:0]),
    .in13(Instruction[2:0]), .in14(Instruction[2:0]), .in15(Instruction[2:0]), .out(Rd_t),
    .sel(Instruction[9:6]));
  Multiplexer #(.enable("false"), .select(4), .width(3)) multiplexer_2 (
    .in0(Instruction[2:0]), .in1(Instruction[2:0]), .in2(Instruction[2:0]), .in3(Instruction[2:0]),
    .in4(Instruction[2:0]), .in5(Instruction[2:0]), .in6(Instruction[2:0]), .in7(Instruction[2:0]),
    .in8(Instruction[2:0]), .in9(Instruction[5:3]), .in10(Instruction[2:0]), .in11(Instruction[2:0]),
    .in12(Instruction[2:0]), .in13(Instruction[5:3]), .in14(Instruction[2:0]), .in15(3'b000), .out(Rn_t),
    .sel(Instruction[9:6]));
  Pull_Resistor pull_resistor_1 (.node(Rd));
  assign Rd = Enable ? Rd_t : 3'bz;  // Controlled_Buffer controlled_buffer_1
  Pull_Resistor pull_resistor_2 (.node(Rn));
  assign Rn = Enable ? Rn_t : 3'bz;  // Controlled_Buffer controlled_buffer_2
  Pull_Resistor pull_resistor_3 (.node(Rm));
  assign Rm = Enable ? Rm_t : 3'bz;  // Controlled_Buffer controlled_buffer_3
  Pull_Resistor pull_resistor_4 (.node(ALU_Opcode));
  assign ALU_Opcode = Enable ? Instruction[9:6] : 4'bz;  // Controlled_Buffer controlled_buffer_4
  Pull_Resistor pull_resistor_5 (.node(Flags_Update_Mask));
  assign Flags_Update_Mask = Enable ? Flags : 4'bz;  // Controlled_Buffer controlled_buffer_5
  Multiplexer #(.enable("false"), .select(4), .width(3)) multiplexer_3 (
    .in0(Instruction[5:3]), .in1(Instruction[5:3]), .in2(Instruction[5:3]), .in3(Instruction[5:3]),
    .in4(Instruction[5:3]), .in5(Instruction[5:3]), .in6(Instruction[5:3]), .in7(Instruction[5:3]),
    .in8(Instruction[5:3]), .in9(3'b000), .in10(Instruction[5:3]), .in11(Instruction[5:3]),
    .in12(Instruction[5:3]), .in13(Instruction[2:0]), .in14(Instruction[5:3]), .in15(Instruction[5:3]),
    .out(Rm_t), .sel(Instruction[9:6]));
  Multiplexer #(.enable("false"), .select(4), .width(4)) multiplexer_4 (
    .in0(4'b1100), .in1(4'b1100), .in2(4'b1110), .in3(4'b1110), .in4(4'b1110), .in5(4'b1111), .in6(4'b1111),
    .in7(4'b1110), .in8(4'b1100), .in9(4'b1100), .in10(4'b1111), .in11(4'b1111), .in12(4'b1100),
    .in13(4'b1100), .in14(4'b1100), .in15(4'b1100), .out(Flags), .sel(Instruction[9:6]));

  // Other names for the same wires on the sheet: A[2:0] = Instruction[2:0]; B[2:0] = Instruction[5:3];
  //   Opcode[3:0] = Instruction[9:6]

  // Notes on the sheet:
  //   Note 2: RSB instruction has Rn as 1st operand.
  //   MUL instruction has Rn as 1st operand and Rdm as 2nd operand
  //   For simplification purposes, Rm is used for 1st operand both here and in the ALU.
  //   Pull output low on Enable = 0
  //   Note: instructions that does not save the result will still have the second operand as the destination register, the ALU will copy the second register to the destination register
endmodule
