// Logisim project Ctl_Flags_APSR.circ as structural Verilog: 1 circuit, main circuit Flags_APSR
module Flags_APSR (
  input  [3:0] Update_Mask,
  input  [3:0] Flags_In,
  input  Clk,
  input  Rst,
  output [3:0] Flags_Out
);

  wire multiplexer_1_out, multiplexer_2_out, multiplexer_3_out, multiplexer_4_out;

  Multiplexer multiplexer_1 (.in0(Flags_Out[0]), .in1(Flags_In[0]), .out(multiplexer_1_out), .sel(Update_Mask[0]));
  Multiplexer multiplexer_2 (.in0(Flags_Out[1]), .in1(Flags_In[1]), .out(multiplexer_2_out), .sel(Update_Mask[1]));
  Multiplexer multiplexer_3 (.in0(Flags_Out[2]), .in1(Flags_In[2]), .out(multiplexer_3_out), .sel(Update_Mask[2]));
  Multiplexer multiplexer_4 (.in0(Flags_Out[3]), .in1(Flags_In[3]), .out(multiplexer_4_out), .sel(Update_Mask[3]));
  D_Flip_Flop d_ff_1 (.D(multiplexer_1_out), .clk(Clk), .Q(Flags_Out[0]), .reset(Rst));  // open: Qn, preset
  D_Flip_Flop d_ff_2 (.D(multiplexer_2_out), .clk(Clk), .Q(Flags_Out[1]), .reset(Rst));  // open: Qn, preset
  D_Flip_Flop d_ff_3 (.D(multiplexer_3_out), .clk(Clk), .Q(Flags_Out[2]), .reset(Rst));  // open: Qn, preset
  D_Flip_Flop d_ff_4 (.D(multiplexer_4_out), .clk(Clk), .Q(Flags_Out[3]), .reset(Rst));  // open: Qn, preset

  // Other names for the same wires on the sheet: clock = Clk; reset = Rst; update[3:0] = Update_Mask;
  //   update_0 = Update_Mask[0]; update_1 = Update_Mask[1]; update_2 = Update_Mask[2]; update_3 = Update_Mask[3]
endmodule
