// Logisim project Ctl_Load_Store.circ as structural Verilog: 1 circuit, main circuit Load_Store
module Load_Store (
  input  Enable,
  input  [15:0] Instruction,
  input  Clk,
  input  Reset,
  input  [31:0] Stack_Pointer,
  output Store,
  output Load,
  output PC_Hold,
  output [2:0] Rmd,
  output [31:0] RAM_Addr
);

  wire and_1_out, Load_t, multiplexer_1_out, not_1_out, not_2_out, PC_Hold_t, xor_1_out;
  wire [31:0] bit_extender_1_out, ram_addr_t;

  assign bit_extender_1_out = {{24{Instruction[7]}}, Instruction[7:0]};  // Bit_Extender bit_extender_1
  Multiplexer multiplexer_1 (.in0(1'b0), .in1(PC_Hold_t), .out(multiplexer_1_out), .sel(Instruction[11]));
  Adder #(.width(32)) adder_1 (.a(Stack_Pointer), .b(bit_extender_1_out), .out(ram_addr_t));  // open: cin, cout
  Pull_Resistor pull_resistor_1 (.node(Store));
  not not_1 (not_1_out, Instruction[11]);
  assign Store = Enable ? not_1_out : 1'bz;  // Controlled_Buffer controlled_buffer_1
  Multiplexer multiplexer_2 (.in0(1'b0), .in1(1'b1), .out(Load), .sel(Instruction[11]));
  Pull_Resistor pull_resistor_2 (.node(PC_Hold));
  assign PC_Hold = Enable ? multiplexer_1_out : 1'bz;  // Controlled_Buffer controlled_buffer_2
  Pull_Resistor pull_resistor_3 (.node(Rmd));
  assign Rmd = Enable ? Instruction[10:8] : 3'bz;  // Controlled_Buffer controlled_buffer_3
  Pull_Resistor pull_resistor_4 (.node(RAM_Addr));
  assign RAM_Addr = Enable ? ram_addr_t : 32'bz;  // Controlled_Buffer controlled_buffer_4
  xor xor_1 (xor_1_out, PC_Hold_t, 1'b1);
  D_Flip_Flop d_ff_1 (.D(xor_1_out), .clk(Clk), .Q(PC_Hold_t));  // open: Qn, preset, reset
  not not_2 (not_2_out, PC_Hold_t);
  D_Flip_Flop d_ff_2 (.D(1'b0), .clk(and_1_out), .Q(Load_t), .reset(Reset));  // open: Qn, preset
  and and_1 (and_1_out, Clk, not_2_out);

  // Other names for the same wires on the sheet: imm8[7:0] = Instruction[7:0]; rmd_t[2:0] = Instruction[10:8];
  //   Bit_11 = Instruction[11]; SP[31:0] = Stack_Pointer

  // Notes on the sheet:
  //   Instruction: pull=down
  //   store / load
  //   Delay load and hold PC for 1 cycle for the RAM to send out requested data 
endmodule
