// Logisim project Ctl_Opcode_Decoder.circ as structural Verilog: 1 circuit, main circuit Opcode_Decoder
module Opcode_Decoder (
  input  [5:0] Opcode,
  output Shift,
  output Data_Processing,
  output Load_Store,
  output SP_Address,
  output Conditional
);

  wire Switch;

  Decoder #(.enable("false"), .select(2)) decoder_1 (
    .out0(Shift), .out1(Data_Processing), .out2(Switch), .out3(Conditional), .sel(Opcode[5:4]));
  Decoder decoder_2 (.out0(Load_Store), .out1(SP_Address), .sel(Opcode[3]), .en(Switch));

  // Other names for the same wires on the sheet: Bit_13 = Opcode[3]; Code[1:0] = Opcode[5:4]; SP_Adress = SP_Address

  // Notes on the sheet:
  //   Shift, add, sub, mov
  //   Load/Store
  //   SP Address
  //   Data Processing
  //   Conditional branch
endmodule
